# Fritzing sketch LED Example (saved by Fritzing 0.9.3b)
breadboards: 1

parts:
  Raspberry_Pi_1 = Raspberry Pi 3 [part_number=RPI-3-V1.2]
  LED1 = LED - 5mm [color="Red (633nm)" package="5 mm [THT]"]
  LED2 = LED - 5mm [color="Yellow (592nm)" package="5 mm [THT]"]
  LED3 = LED - 5mm [color="Green (565nm)" package="5 mm [THT]"]
  R1 = Resistor [tolerance=±5% resistance=330 package=THT]
  R2 = Resistor [tolerance=±5% resistance=330 package=THT]
  R3 = Resistor [tolerance=±5% resistance=330 package=THT]

nets:
  N1: Raspberry_Pi_1.GPIO26, LED2.anode
  N2: Raspberry_Pi_1.GND, R1.Pin_1, R2.Pin_1, R3.Pin_1
  N3: Raspberry_Pi_1.GPIO21, LED1.anode
  N4: Raspberry_Pi_1.GPIO18, LED3.anode
  N5: LED1.cathode, R1.Pin_0
  N6: LED2.cathode, R2.Pin_0
  N7: LED3.cathode, R3.Pin_0
